// Logisim project Part 2.1.circ as structural Verilog: 5 circuits, main circuit 1 bit alu
module _1_bit_alu (
  input  Cin,
  input  A,
  input  B,
  input  [2:0] in_4,
  input  Bin,
  output res,
  output cout
);

  wire adder_1_cout, adder_1_out, adder_2_cout, adder_2_out, and_1_out, not_1_out, not_2_out, or_1_out,
       xor_1_out;

  and and_1 (and_1_out, A, B);
  or or_1 (or_1_out, A, B);
  xor xor_1 (xor_1_out, B, Bin);
  not not_1 (not_1_out, and_1_out);
  not not_2 (not_2_out, or_1_out);
  Adder #(.width(1)) adder_1 (.a(A), .b(xor_1_out), .out(adder_1_out), .cin(Cin), .cout(adder_1_cout));
  Adder #(.width(1)) adder_2 (.a(A), .b(B), .out(adder_2_out), .cin(Cin), .cout(adder_2_cout));
  Multiplexer #(.select(3)) multiplexer_1 (
    .in0(and_1_out), .in1(or_1_out), .in2(adder_2_out), .in3(not_1_out), .in4(not_2_out), .in5(1'b0),
    .in6(adder_1_out), .in7(1'b0), .out(res), .sel(in_4));  // open: en
  Multiplexer #(.select(3)) multiplexer_2 (
    .in0(1'b0), .in1(1'b0), .in2(adder_2_cout), .in3(1'b0), .in4(1'b0), .in5(1'b0), .in6(adder_1_cout),
    .in7(1'b0), .out(cout), .sel(in_4));  // open: en
endmodule

module multiplier (
  input  in_1,
  input  in_2,
  input  in_3,
  input  in_4,
  input  in_5,
  input  in_6,
  input  in_7,
  input  in_8,
  input  in_9,
  input  in_10,
  input  in_11,
  input  in_12,
  output [11:0] out_13,
  output out_14
);

  wire [4:0] and_12_out;
  wire [5:0] adder_1_out, adder_2_out, adder_3_out, adder_5_out, and_24_out, and_25_out, and_27_out,
       and_34_out, and_36_out;

  and and_1 (and_12_out[4], in_1, in_12);
  and and_2 (and_12_out[3], in_1, in_11);
  and and_3 (and_12_out[2], in_1, in_10);
  and and_4 (and_24_out[5], in_3, in_12);
  and and_5 (and_25_out[5], in_4, in_12);
  and and_6 (and_12_out[1], in_1, in_9);
  and and_7 (and_24_out[3], in_3, in_10);
  and and_8 (and_24_out[4], in_3, in_11);
  and and_9 (and_25_out[4], in_4, in_11);
  and and_10 (and_27_out[5], in_5, in_12);
  and and_11 (and_27_out[4], in_5, in_11);
  and and_12 (and_12_out[0], in_1, in_8);
  and and_13 (and_24_out[2], in_3, in_9);
  and and_14 (and_25_out[3], in_4, in_10);
  and and_15 (and_27_out[3], in_5, in_10);
  and and_16 (and_24_out[1], in_3, in_8);
  and and_17 (and_25_out[1], in_4, in_8);
  and and_18 (and_25_out[2], in_4, in_9);
  and and_19 (and_27_out[2], in_5, in_9);
  and and_20 (and_34_out[4], in_6, in_11);
  and and_21 (and_34_out[5], in_6, in_12);
  and and_22 (out_13[0], in_1, in_7);
  and and_23 (and_36_out[5], in_2, in_12);
  and and_24 (and_24_out[0], in_3, in_7);
  and and_25 (and_25_out[0], in_4, in_7);
  and and_26 (and_27_out[1], in_5, in_8);
  and and_27 (and_27_out[0], in_5, in_7);
  and and_28 (and_34_out[3], in_6, in_10);
  and and_29 (and_36_out[4], in_2, in_11);
  and and_30 (and_34_out[2], in_6, in_9);
  and and_31 (and_36_out[2], in_2, in_9);
  and and_32 (and_36_out[3], in_2, in_10);
  and and_33 (and_34_out[1], in_6, in_8);
  and and_34 (and_34_out[0], in_6, in_7);
  and and_35 (and_36_out[1], in_2, in_8);
  and and_36 (and_36_out[0], in_2, in_7);
  Adder #(.width(6)) adder_1 (
    .a({1'b0, and_12_out}), .b(and_36_out), .out({adder_1_out[4:0], out_13[1]}), .cout(adder_1_out[5]));  // open: cin
  Adder #(.width(6)) adder_2 (
    .a(adder_1_out), .b(and_24_out), .out({adder_2_out[4:0], out_13[2]}), .cout(adder_2_out[5]));  // open: cin
  Adder #(.width(6)) adder_3 (
    .a(adder_5_out), .b(and_27_out), .out({adder_3_out[4:0], out_13[4]}), .cout(adder_3_out[5]));  // open: cin
  Adder #(.width(6)) adder_4 (.a(adder_3_out), .b(and_34_out), .out(out_13[10:5]), .cout(out_13[11]));  // open: cin
  Adder #(.width(6)) adder_5 (
    .a(adder_2_out), .b(and_25_out), .out({adder_5_out[4:0], out_13[3]}), .cout(adder_5_out[5]));  // open: cin
  xor xor_1 (out_14, adder_3_out[5], out_13[11]);

  // Other names for the same wires on the sheet: A0 = in_1; A1 = in_2; A2 = in_3; A3 = in_4; A4 = in_5; A5 = in_6;
  //   B0 = in_7; B1 = in_8; B2 = in_9; B3 = in_10; B4 = in_11; B5 = in_12
endmodule

module _12_bit_alu (
  input  [11:0] in_1,
  input  in_2,
  input  in_3,
  input  in_4,
  input  in_5,
  input  in_6,
  input  [11:0] in_7,
  output [11:0] RESULT,
  output ZERO,
  output OVERFLOW,
  output out_11
);

  wire and_2_out, multiplexer_1_out, mux, n1_bit_alu_1_cout, n1_bit_alu_2_cout, n1_bit_alu_3_cout,
       n1_bit_alu_4_cout, n1_bit_alu_5_cout, n1_bit_alu_6_cout, n1_bit_alu_7_cout, n1_bit_alu_8_cout,
       n1_bit_alu_9_cout, n1_bit_alu_10_cout, n1_bit_alu_11_cout, not_1_out, ov, xor_1_out;
  wire [2:0] sel;
  wire [11:0] multiplier_1_out_13, n1_bit_alu_1_res;

  Control_Circuit control_circuit_1 (
    .X(sel[2]), .Y(sel[1]), .Z(sel[0]), .Aluop0(in_2), .Aluop1(in_3), .Aluop2(in_4), .F1(in_5), .f0(in_6));
  and and_1 (mux, sel[2], sel[1], sel[0]);
  multiplier multiplier_1 (
    .in_1(in_1[0]), .in_2(in_1[1]), .in_3(in_1[2]), .in_4(in_1[3]), .out_13(multiplier_1_out_13),
    .in_5(in_1[4]), .in_6(in_1[5]), .in_7(in_7[0]), .in_8(in_7[1]), .in_9(in_7[2]), .in_10(in_7[3]),
    .in_11(in_7[4]), .in_12(in_7[5]), .out_14(ov));
  not not_1 (not_1_out, sel[0]);
  and and_2 (and_2_out, sel[2], sel[1], not_1_out);
  Multiplexer multiplexer_1 (.in0(1'b0), .in1(1'b1), .out(multiplexer_1_out), .sel(and_2_out));  // open: en
  _1_bit_alu u_1_bit_alu_1 (
    .Bin(and_2_out), .res(n1_bit_alu_1_res[0]), .cout(n1_bit_alu_1_cout), .B(in_7[0]), .A(in_1[0]),
    .Cin(multiplexer_1_out), .in_4(sel));
  _1_bit_alu u_1_bit_alu_2 (
    .Bin(and_2_out), .res(n1_bit_alu_1_res[1]), .cout(n1_bit_alu_2_cout), .B(in_7[1]), .A(in_1[1]),
    .Cin(n1_bit_alu_1_cout), .in_4(sel));
  _1_bit_alu u_1_bit_alu_3 (
    .Bin(and_2_out), .res(n1_bit_alu_1_res[2]), .cout(n1_bit_alu_3_cout), .B(in_7[2]), .A(in_1[2]),
    .Cin(n1_bit_alu_2_cout), .in_4(sel));
  _1_bit_alu u_1_bit_alu_4 (
    .Bin(and_2_out), .res(n1_bit_alu_1_res[3]), .cout(n1_bit_alu_4_cout), .B(in_7[3]), .A(in_1[3]),
    .Cin(n1_bit_alu_3_cout), .in_4(sel));
  _1_bit_alu u_1_bit_alu_5 (
    .Bin(and_2_out), .res(n1_bit_alu_1_res[4]), .cout(n1_bit_alu_5_cout), .B(in_7[4]), .A(in_1[4]),
    .Cin(n1_bit_alu_4_cout), .in_4(sel));
  _1_bit_alu u_1_bit_alu_6 (
    .Bin(and_2_out), .res(n1_bit_alu_1_res[5]), .cout(n1_bit_alu_6_cout), .B(in_7[5]), .A(in_1[5]),
    .Cin(n1_bit_alu_5_cout), .in_4(sel));
  _1_bit_alu u_1_bit_alu_7 (
    .Bin(and_2_out), .res(n1_bit_alu_1_res[6]), .cout(n1_bit_alu_7_cout), .B(in_7[6]), .A(in_1[6]),
    .Cin(n1_bit_alu_6_cout), .in_4(sel));
  _1_bit_alu u_1_bit_alu_8 (
    .Bin(and_2_out), .res(n1_bit_alu_1_res[7]), .cout(n1_bit_alu_8_cout), .B(in_7[7]), .A(in_1[7]),
    .Cin(n1_bit_alu_7_cout), .in_4(sel));
  _1_bit_alu u_1_bit_alu_9 (
    .Bin(and_2_out), .res(n1_bit_alu_1_res[8]), .cout(n1_bit_alu_9_cout), .B(in_7[8]), .A(in_1[8]),
    .Cin(n1_bit_alu_8_cout), .in_4(sel));
  _1_bit_alu u_1_bit_alu_10 (
    .Bin(and_2_out), .res(n1_bit_alu_1_res[9]), .cout(n1_bit_alu_10_cout), .B(in_7[9]), .A(in_1[9]),
    .Cin(n1_bit_alu_9_cout), .in_4(sel));
  _1_bit_alu u_1_bit_alu_11 (
    .Bin(and_2_out), .res(n1_bit_alu_1_res[10]), .cout(n1_bit_alu_11_cout), .B(in_7[10]), .A(in_1[10]),
    .Cin(n1_bit_alu_10_cout), .in_4(sel));
  _1_bit_alu u_1_bit_alu_12 (
    .Bin(and_2_out), .res(n1_bit_alu_1_res[11]), .cout(out_11), .B(in_7[11]), .A(in_1[11]),
    .Cin(n1_bit_alu_11_cout), .in_4(sel));
  xor xor_1 (xor_1_out, n1_bit_alu_11_cout, out_11);
  Multiplexer multiplexer_2 (.in0(xor_1_out), .in1(ov), .out(OVERFLOW), .sel(mux));  // open: en
  Multiplexer #(.width(12)) multiplexer_3 (
    .in0(n1_bit_alu_1_res), .in1(multiplier_1_out_13), .out(RESULT), .sel(mux));  // open: en
  or or_1 (ZERO, RESULT[0], RESULT[1], RESULT[2], RESULT[3], RESULT[4], RESULT[5], RESULT[6], RESULT[7], RESULT[8], RESULT[9], RESULT[10], RESULT[11]);

  // Other names for the same wires on the sheet: _1 = in_1[0]; _2 = in_1[1]; _3 = in_1[2]; _4 = in_1[3]; _5 = in_1[4];
  //   _6 = in_1[5]; _7 = in_1[6]; _8 = in_1[7]; _9 = in_1[8]; _10 = in_1[9]; _11 = in_1[10]; _12 = in_1[11];
  //   a = in_7[0]; b = in_7[1]; c = in_7[2]; d = in_7[3]; e = in_7[4]; f = in_7[5]; g = in_7[6]; h = in_7[7];
  //   i = in_7[8]; j = in_7[9]; k = in_7[10]; m = in_7[11]
endmodule

module Control_Circuit (
  input  Aluop0,
  input  Aluop1,
  input  Aluop2,
  input  F1,
  input  f0,
  output X,
  output Y,
  output Z
);

  wire nand_1_out, nand_2_out, nand_3_out, nand_4_out, nand_5_out, nand_6_out, nand_7_out, nand_8_out,
       nand_9_out, nand_10_out, nand_11_out, nand_12_out, nand_13_out, nand_14_out, nand_15_out;

  nand nand_1 (nand_1_out, Aluop0, Aluop0);
  nand nand_2 (nand_2_out, Aluop1, Aluop1);
  nand nand_3 (nand_3_out, Aluop2, Aluop2);
  nand nand_4 (nand_4_out, f0, f0);
  nand nand_5 (nand_5_out, F1, F1);
  nand nand_6 (nand_6_out, f0, f0);
  nand nand_7 (nand_7_out, Aluop1, Aluop1);
  nand nand_8 (nand_8_out, Aluop2, Aluop2);
  nand nand_9 (nand_9_out, nand_1_out, nand_2_out, nand_3_out, F1, f0);
  nand nand_10 (nand_10_out, nand_1_out, Aluop1, nand_3_out, F1, nand_4_out);
  nand nand_11 (nand_11_out, nand_1_out, Aluop1, Aluop2, F1, f0);
  nand nand_12 (nand_12_out, nand_1_out, nand_2_out, nand_3_out, nand_5_out, nand_4_out);
  nand nand_13 (nand_13_out, nand_1_out, Aluop1, F1, nand_6_out);
  nand nand_14 (nand_14_out, nand_1_out, Aluop1, Aluop2, F1, nand_6_out);
  nand nand_15 (nand_15_out, nand_1_out, nand_7_out, nand_8_out, F1);
  nand nand_16 (X, nand_9_out, nand_10_out, nand_11_out);
  nand nand_17 (Y, nand_12_out, nand_9_out, nand_13_out);
  nand nand_18 (Z, nand_14_out, nand_15_out);
endmodule

module data (
  input  Clear,
  output [11:0] out_2,
  output [3:0] op,
  output [11:0] out_4,
  output [1:0] rd,
  output [1:0] rs,
  output [1:0] rt,
  output [1:0] fun,
  output [3:0] out_9
);

  wire Clock_out;
  wire [11:0] register_1_q;

  Register #(.width(12)) register_1 (.D(out_4), .Q(register_1_q), .clk(Clock_out), .clr(Clear));  // open: en
  Clock Clock (.out(Clock_out));
  Adder #(.width(12)) adder_1 (.a(12'h2), .b(register_1_q), .out(out_4));  // open: cin, cout
  ROM #(.addrWidth(12), .dataWidth(12)) rom_1 (.addr(register_1_q), .data({op, out_2[7:2], fun}), .sel(1'b1));

  assign {out_2[11:8], out_2[1:0]} = {op, fun};
  assign out_9 = {fun, out_2[5:4]};
  assign rd = out_2[7:6];
  assign rs = out_2[5:4];
  assign rt = out_2[3:2];

  // Notes on the sheet:
  //   Selection
  //   contents of rom_1 (hex, n*v repeats v):
  //   6*0 9a
  //   imme
endmodule
