// Logisim project Project Part 03.circ as structural Verilog: 14 circuits, main circuit 1 bit alu
module _1_bit_alu (
  input  Cin,
  input  A,
  input  B,
  input  [2:0] in_4,
  input  Bin,
  output res,
  output cout
);

  wire adder_1_cout, adder_1_out, adder_2_cout, adder_2_out, and_1_out, not_1_out, not_2_out, or_1_out,
       xor_1_out;

  and and_1 (and_1_out, A, B);
  or or_1 (or_1_out, A, B);
  xor xor_1 (xor_1_out, B, Bin);
  not not_1 (not_1_out, and_1_out);
  not not_2 (not_2_out, or_1_out);
  Adder #(.width(1)) adder_1 (.a(A), .b(xor_1_out), .out(adder_1_out), .cin(Cin), .cout(adder_1_cout));
  Adder #(.width(1)) adder_2 (.a(A), .b(B), .out(adder_2_out), .cin(Cin), .cout(adder_2_cout));
  Multiplexer #(.select(3)) multiplexer_1 (
    .in0(and_1_out), .in1(or_1_out), .in2(adder_2_out), .in3(not_1_out), .in4(not_2_out), .in5(1'b0),
    .in6(adder_1_out), .in7(1'b0), .out(res), .sel(in_4));  // open: en
  Multiplexer #(.select(3)) multiplexer_2 (
    .in0(1'b0), .in1(1'b0), .in2(adder_2_cout), .in3(1'b0), .in4(1'b0), .in5(1'b0), .in6(adder_1_cout),
    .in7(1'b0), .out(cout), .sel(in_4));  // open: en
endmodule

module multiplier (
  input  in_1,
  input  in_2,
  input  in_3,
  input  in_4,
  input  in_5,
  input  in_6,
  input  in_7,
  input  in_8,
  input  in_9,
  input  in_10,
  input  in_11,
  input  in_12,
  output [11:0] out_13,
  output out_14
);

  wire [4:0] and_12_out;
  wire [5:0] adder_1_out, adder_2_out, adder_3_out, adder_5_out, and_24_out, and_25_out, and_26_out,
       and_33_out, and_36_out;

  and and_1 (and_12_out[4], in_1, in_12);
  and and_2 (and_12_out[3], in_1, in_11);
  and and_3 (and_12_out[2], in_1, in_10);
  and and_4 (and_24_out[5], in_3, in_12);
  and and_5 (and_25_out[5], in_4, in_12);
  and and_6 (and_12_out[1], in_1, in_9);
  and and_7 (and_24_out[4], in_3, in_11);
  and and_8 (and_24_out[3], in_3, in_10);
  and and_9 (and_25_out[4], in_4, in_11);
  and and_10 (and_26_out[5], in_5, in_12);
  and and_11 (and_26_out[4], in_5, in_11);
  and and_12 (and_12_out[0], in_1, in_8);
  and and_13 (and_24_out[2], in_3, in_9);
  and and_14 (and_25_out[3], in_4, in_10);
  and and_15 (and_26_out[3], in_5, in_10);
  and and_16 (and_24_out[1], in_3, in_8);
  and and_17 (and_25_out[1], in_4, in_8);
  and and_18 (and_25_out[2], in_4, in_9);
  and and_19 (and_26_out[2], in_5, in_9);
  and and_20 (and_33_out[5], in_6, in_12);
  and and_21 (and_33_out[4], in_6, in_11);
  and and_22 (out_13[0], in_1, in_7);
  and and_23 (and_36_out[5], in_2, in_12);
  and and_24 (and_24_out[0], in_3, in_7);
  and and_25 (and_25_out[0], in_4, in_7);
  and and_26 (and_26_out[0], in_5, in_7);
  and and_27 (and_26_out[1], in_5, in_8);
  and and_28 (and_33_out[3], in_6, in_10);
  and and_29 (and_36_out[4], in_2, in_11);
  and and_30 (and_33_out[2], in_6, in_9);
  and and_31 (and_36_out[3], in_2, in_10);
  and and_32 (and_36_out[2], in_2, in_9);
  and and_33 (and_33_out[0], in_6, in_7);
  and and_34 (and_33_out[1], in_6, in_8);
  and and_35 (and_36_out[1], in_2, in_8);
  and and_36 (and_36_out[0], in_2, in_7);
  Adder #(.width(6)) adder_1 (
    .a({1'b0, and_12_out}), .b(and_36_out), .out({adder_1_out[4:0], out_13[1]}), .cout(adder_1_out[5]));  // open: cin
  Adder #(.width(6)) adder_2 (
    .a(adder_1_out), .b(and_24_out), .out({adder_2_out[4:0], out_13[2]}), .cout(adder_2_out[5]));  // open: cin
  Adder #(.width(6)) adder_3 (
    .a(adder_5_out), .b(and_26_out), .out({adder_3_out[4:0], out_13[4]}), .cout(adder_3_out[5]));  // open: cin
  Adder #(.width(6)) adder_4 (.a(adder_3_out), .b(and_33_out), .out(out_13[10:5]), .cout(out_13[11]));  // open: cin
  Adder #(.width(6)) adder_5 (
    .a(adder_2_out), .b(and_25_out), .out({adder_5_out[4:0], out_13[3]}), .cout(adder_5_out[5]));  // open: cin
  xor xor_1 (out_14, adder_3_out[5], out_13[11]);

  // Other names for the same wires on the sheet: A0 = in_1; A1 = in_2; A2 = in_3; A3 = in_4; A4 = in_5; A5 = in_6;
  //   B0 = in_7; B1 = in_8; B2 = in_9; B3 = in_10; B4 = in_11; B5 = in_12
endmodule

// ALU
module _12_bit_alu (
  input  [11:0] in_1,
  input  in_2,
  input  in_3,
  input  in_4,
  input  in_5,
  input  in_6,
  input  [11:0] in_7,
  output [11:0] RESULT,
  output ZERO,
  output OVERFLOW,
  output out_11
);

  wire and_2_out, multiplexer_1_out, mux, n1_bit_alu_1_cout, n1_bit_alu_2_cout, n1_bit_alu_3_cout,
       n1_bit_alu_4_cout, n1_bit_alu_5_cout, n1_bit_alu_6_cout, n1_bit_alu_7_cout, n1_bit_alu_8_cout,
       n1_bit_alu_9_cout, n1_bit_alu_10_cout, n1_bit_alu_11_cout, not_1_out, ov, xor_1_out;
  wire [2:0] sel;
  wire [11:0] multiplier_1_out_13, n1_bit_alu_1_res;

  Control_Circuit control_circuit_1 (
    .X(sel[2]), .Y(sel[1]), .Z(sel[0]), .Aluop0(in_2), .Aluop1(in_3), .Aluop2(in_4), .F1(in_5), .f0(in_6));
  and and_1 (mux, sel[2], sel[1], sel[0]);
  multiplier multiplier_1 (
    .in_1(in_1[0]), .in_2(in_1[1]), .in_3(in_1[2]), .in_4(in_1[3]), .out_13(multiplier_1_out_13),
    .in_5(in_1[4]), .in_6(in_1[5]), .in_7(in_7[0]), .in_8(in_7[1]), .in_9(in_7[2]), .in_10(in_7[3]),
    .in_11(in_7[4]), .in_12(in_7[5]), .out_14(ov));
  not not_1 (not_1_out, sel[0]);
  and and_2 (and_2_out, sel[2], sel[1], not_1_out);
  Multiplexer multiplexer_1 (.in0(1'b0), .in1(1'b1), .out(multiplexer_1_out), .sel(and_2_out));  // open: en
  _1_bit_alu u_1_bit_alu_1 (
    .Bin(and_2_out), .res(n1_bit_alu_1_res[0]), .cout(n1_bit_alu_1_cout), .B(in_7[0]), .A(in_1[0]),
    .Cin(multiplexer_1_out), .in_4(sel));
  _1_bit_alu u_1_bit_alu_2 (
    .Bin(and_2_out), .res(n1_bit_alu_1_res[1]), .cout(n1_bit_alu_2_cout), .B(in_7[1]), .A(in_1[1]),
    .Cin(n1_bit_alu_1_cout), .in_4(sel));
  _1_bit_alu u_1_bit_alu_3 (
    .Bin(and_2_out), .res(n1_bit_alu_1_res[2]), .cout(n1_bit_alu_3_cout), .B(in_7[2]), .A(in_1[2]),
    .Cin(n1_bit_alu_2_cout), .in_4(sel));
  _1_bit_alu u_1_bit_alu_4 (
    .Bin(and_2_out), .res(n1_bit_alu_1_res[3]), .cout(n1_bit_alu_4_cout), .B(in_7[3]), .A(in_1[3]),
    .Cin(n1_bit_alu_3_cout), .in_4(sel));
  _1_bit_alu u_1_bit_alu_5 (
    .Bin(and_2_out), .res(n1_bit_alu_1_res[4]), .cout(n1_bit_alu_5_cout), .B(in_7[4]), .A(in_1[4]),
    .Cin(n1_bit_alu_4_cout), .in_4(sel));
  _1_bit_alu u_1_bit_alu_6 (
    .Bin(and_2_out), .res(n1_bit_alu_1_res[5]), .cout(n1_bit_alu_6_cout), .B(in_7[5]), .A(in_1[5]),
    .Cin(n1_bit_alu_5_cout), .in_4(sel));
  _1_bit_alu u_1_bit_alu_7 (
    .Bin(and_2_out), .res(n1_bit_alu_1_res[6]), .cout(n1_bit_alu_7_cout), .B(in_7[6]), .A(in_1[6]),
    .Cin(n1_bit_alu_6_cout), .in_4(sel));
  _1_bit_alu u_1_bit_alu_8 (
    .Bin(and_2_out), .res(n1_bit_alu_1_res[7]), .cout(n1_bit_alu_8_cout), .B(in_7[7]), .A(in_1[7]),
    .Cin(n1_bit_alu_7_cout), .in_4(sel));
  _1_bit_alu u_1_bit_alu_9 (
    .Bin(and_2_out), .res(n1_bit_alu_1_res[8]), .cout(n1_bit_alu_9_cout), .B(in_7[8]), .A(in_1[8]),
    .Cin(n1_bit_alu_8_cout), .in_4(sel));
  _1_bit_alu u_1_bit_alu_10 (
    .Bin(and_2_out), .res(n1_bit_alu_1_res[9]), .cout(n1_bit_alu_10_cout), .B(in_7[9]), .A(in_1[9]),
    .Cin(n1_bit_alu_9_cout), .in_4(sel));
  _1_bit_alu u_1_bit_alu_11 (
    .Bin(and_2_out), .res(n1_bit_alu_1_res[10]), .cout(n1_bit_alu_11_cout), .B(in_7[10]), .A(in_1[10]),
    .Cin(n1_bit_alu_10_cout), .in_4(sel));
  _1_bit_alu u_1_bit_alu_12 (
    .Bin(and_2_out), .res(n1_bit_alu_1_res[11]), .cout(out_11), .B(in_7[11]), .A(in_1[11]),
    .Cin(n1_bit_alu_11_cout), .in_4(sel));
  xor xor_1 (xor_1_out, n1_bit_alu_11_cout, out_11);
  Multiplexer multiplexer_2 (.in0(xor_1_out), .in1(ov), .out(OVERFLOW), .sel(mux));  // open: en
  Multiplexer #(.width(12)) multiplexer_3 (
    .in0(n1_bit_alu_1_res), .in1(multiplier_1_out_13), .out(RESULT), .sel(mux));  // open: en
  or or_1 (ZERO, RESULT[0], RESULT[1], RESULT[2], RESULT[3], RESULT[4], RESULT[5], RESULT[6], RESULT[7], RESULT[8], RESULT[9], RESULT[10], RESULT[11]);

  // Other names for the same wires on the sheet: _1 = in_1[0]; _2 = in_1[1]; _3 = in_1[2]; _4 = in_1[3]; _5 = in_1[4];
  //   _6 = in_1[5]; _7 = in_1[6]; _8 = in_1[7]; _9 = in_1[8]; _10 = in_1[9]; _11 = in_1[10]; _12 = in_1[11];
  //   a = in_7[0]; b = in_7[1]; c = in_7[2]; d = in_7[3]; e = in_7[4]; f = in_7[5]; g = in_7[6]; h = in_7[7];
  //   i = in_7[8]; j = in_7[9]; k = in_7[10]; m = in_7[11]
endmodule

module Control_Circuit (
  input  Aluop0,
  input  Aluop1,
  input  Aluop2,
  input  F1,
  input  f0,
  output X,
  output Y,
  output Z
);

  wire nand_1_out, nand_2_out, nand_3_out, nand_4_out, nand_5_out, nand_6_out, nand_7_out, nand_8_out,
       nand_9_out, nand_10_out, nand_11_out, nand_12_out, nand_13_out, nand_14_out, nand_15_out;

  nand nand_1 (nand_1_out, Aluop0, Aluop0);
  nand nand_2 (nand_2_out, Aluop1, Aluop1);
  nand nand_3 (nand_3_out, Aluop2, Aluop2);
  nand nand_4 (nand_4_out, f0, f0);
  nand nand_5 (nand_5_out, F1, F1);
  nand nand_6 (nand_6_out, f0, f0);
  nand nand_7 (nand_7_out, Aluop1, Aluop1);
  nand nand_8 (nand_8_out, Aluop2, Aluop2);
  nand nand_9 (nand_9_out, nand_1_out, nand_2_out, nand_3_out, F1, f0);
  nand nand_10 (nand_10_out, nand_1_out, Aluop1, nand_3_out, F1, nand_4_out);
  nand nand_11 (nand_11_out, nand_1_out, Aluop1, Aluop2, F1, f0);
  nand nand_12 (nand_12_out, nand_1_out, nand_2_out, nand_3_out, nand_5_out, nand_4_out);
  nand nand_13 (nand_13_out, nand_1_out, Aluop1, F1, nand_6_out);
  nand nand_14 (nand_14_out, nand_1_out, Aluop1, Aluop2, F1, nand_6_out);
  nand nand_15 (nand_15_out, nand_1_out, nand_7_out, nand_8_out, F1);
  nand nand_16 (X, nand_9_out, nand_10_out, nand_11_out);
  nand nand_17 (Y, nand_12_out, nand_9_out, nand_13_out);
  nand nand_18 (Z, nand_14_out, nand_15_out);
endmodule

module register (
  input  in_1,
  input  [2:0] in_2,
  input  [2:0] in_3,
  input  [11:0] in_4,
  input  in_5,
  input  [2:0] in_6,
  output [11:0] out_7,
  output [11:0] out_8
);

  wire decoder_1_out0, decoder_1_out1, decoder_1_out2, decoder_1_out3, decoder_1_out4, decoder_1_out5,
       decoder_1_out6, decoder_1_out7, undriven;
  wire [11:0] multiplexer_1_out, register_1_q, register_2_q, register_3_q, register_4_q, register_5_q,
       register_6_q, register_7_q, register_8_q;

  Decoder #(.select(3)) decoder_1 (
    .out0(decoder_1_out0), .out1(decoder_1_out1), .out2(decoder_1_out2), .out3(decoder_1_out3),
    .out4(decoder_1_out4), .out5(decoder_1_out5), .out6(decoder_1_out6), .out7(decoder_1_out7), .sel(in_3),
    .en(undriven));
  Multiplexer #(.width(12)) multiplexer_1 (.in1(in_4), .out(multiplexer_1_out), .sel(in_5));  // open: in0, en
  Register #(.width(12)) register_1 (
    .D(multiplexer_1_out), .en(decoder_1_out0), .Q(register_1_q), .clk(in_1));  // open: clr
  Register #(.width(12)) register_2 (
    .D(multiplexer_1_out), .en(decoder_1_out1), .Q(register_2_q), .clk(in_1));  // open: clr
  Register #(.width(12)) register_3 (
    .D(multiplexer_1_out), .en(decoder_1_out2), .Q(register_3_q), .clk(in_1));  // open: clr
  Register #(.width(12)) register_4 (
    .D(multiplexer_1_out), .en(decoder_1_out3), .Q(register_4_q), .clk(in_1));  // open: clr
  Register #(.width(12)) register_5 (
    .D(multiplexer_1_out), .en(decoder_1_out4), .Q(register_5_q), .clk(in_1));  // open: clr
  Register #(.width(12)) register_6 (
    .D(multiplexer_1_out), .en(decoder_1_out5), .Q(register_6_q), .clk(in_1));  // open: clr
  Register #(.width(12)) register_7 (
    .D(multiplexer_1_out), .en(decoder_1_out6), .Q(register_7_q), .clk(in_1));  // open: clr
  Register #(.width(12)) register_8 (
    .D(multiplexer_1_out), .en(decoder_1_out7), .Q(register_8_q), .clk(in_1));  // open: clr
  Multiplexer #(.select(3), .width(12)) multiplexer_2 (
    .in0(register_1_q), .in1(register_2_q), .in2(register_3_q), .in3(register_4_q), .in4(register_5_q),
    .in5(register_6_q), .in6(register_7_q), .in7(register_8_q), .out(out_7), .sel(in_2));  // open: en
  Multiplexer #(.select(3), .width(12)) multiplexer_3 (
    .in0(register_1_q), .in1(register_2_q), .in2(register_3_q), .in3(register_4_q), .in4(register_5_q),
    .in5(register_6_q), .in6(register_7_q), .in7(register_8_q), .out(out_8), .sel(in_6));  // open: en
endmodule

// Register File
module \reg  (
  input  in_1,
  input  [1:0] in_2,
  input  [1:0] in_3,
  input  [11:0] in_4,
  input  in_5,
  input  [1:0] in_6,
  output [11:0] out_7,
  output [11:0] out_8
);

  wire decoder_1_out0, decoder_1_out1, decoder_1_out2, decoder_1_out3;
  wire [11:0] multiplexer_1_out, Register_01_q, Register_02_q, Register_03_q, Register_04_q;

  Decoder #(.select(2)) decoder_1 (
    .out0(decoder_1_out0), .out1(decoder_1_out1), .out2(decoder_1_out2), .out3(decoder_1_out3), .sel(in_2));  // open: en
  Multiplexer #(.width(12)) multiplexer_1 (.in1(in_4), .out(multiplexer_1_out), .sel(in_5));  // open: in0, en
  Register #(.width(12)) Register_01 (
    .D(multiplexer_1_out), .en(decoder_1_out0), .Q(Register_01_q), .clk(in_1));  // open: clr
  Register #(.width(12)) Register_02 (
    .D(multiplexer_1_out), .en(decoder_1_out1), .Q(Register_02_q), .clk(in_1));  // open: clr
  Register #(.width(12)) Register_03 (
    .D(multiplexer_1_out), .en(decoder_1_out2), .Q(Register_03_q), .clk(in_1));  // open: clr
  Register #(.width(12)) Register_04 (
    .D(multiplexer_1_out), .en(decoder_1_out3), .Q(Register_04_q), .clk(in_1));  // open: clr
  Multiplexer #(.select(2), .width(12)) multiplexer_2 (
    .in0(Register_01_q), .in1(Register_02_q), .in2(Register_03_q), .in3(Register_04_q), .out(out_7),
    .sel(in_3));  // open: en
  Multiplexer #(.select(2), .width(12)) multiplexer_3 (
    .in0(Register_01_q), .in1(Register_02_q), .in2(Register_03_q), .in3(Register_04_q), .out(out_8),
    .sel(in_6));  // open: en
endmodule

module controlunit (
  input  a,
  input  b,
  input  c,
  output regdes,
  output aludes,
  output regwrite,
  output ld,
  output str,
  output memreg,
  output bin,
  output jump,
  output addi
);

  wire and_3_out, and_4_out, and_5_out, and_6_out, and_7_out, and_8_out, and_9_out, and_10_out, and_11_out,
       and_12_out, not_1_out, not_2_out, not_3_out, not_4_out, not_5_out, not_6_out, not_7_out, not_8_out,
       not_9_out, not_10_out, not_11_out;

  not not_1 (not_1_out, b);
  not not_2 (not_2_out, c);
  not not_3 (not_3_out, b);
  not not_4 (not_4_out, b);
  not not_5 (not_5_out, c);
  not not_6 (not_6_out, b);
  not not_7 (not_7_out, b);
  not not_8 (not_8_out, b);
  not not_9 (not_9_out, b);
  not not_10 (not_10_out, b);
  not not_11 (not_11_out, c);
  not not_12 (memreg, b);
  and and_1 (bin, b, c);
  and and_2 (jump, b, c);
  and and_3 (and_3_out, not_1_out, c);
  and and_4 (and_4_out, b, not_2_out);
  and and_5 (and_5_out, a, not_3_out);
  and and_6 (and_6_out, not_4_out, c);
  and and_7 (and_7_out, b, not_5_out);
  and and_8 (and_8_out, a, not_6_out);
  and and_9 (and_9_out, not_7_out, c);
  and and_10 (and_10_out, a, not_8_out);
  and and_11 (and_11_out, not_9_out, c);
  and and_12 (and_12_out, a, not_10_out);
  and and_13 (str, b, not_11_out);
  or or_1 (regdes, and_3_out, and_4_out, and_5_out);
  or or_2 (aludes, and_6_out, and_7_out, and_8_out);
  or or_3 (regwrite, and_9_out, and_10_out);
  or or_4 (ld, and_11_out, and_12_out);

  assign addi = a;
endmodule

// Instruction Fetch
module IF (
  input  [11:0] in_1,
  input  pcsrc,
  input  Clock,
  input  Reset,
  output [11:0] out_5
);

  wire [11:0] adder_1_out, multiplexer_1_out, Pc_q;

  Multiplexer #(.width(12)) multiplexer_1 (
    .in0(adder_1_out), .in1(in_1), .out(multiplexer_1_out), .sel(pcsrc));  // open: en
  Register #(.width(12)) Pc (.D(multiplexer_1_out), .Q(Pc_q), .clk(Clock), .clr(Reset));  // open: en
  Adder #(.width(12)) adder_1 (.a(12'h2), .b(Pc_q), .out(adder_1_out));  // open: cin, cout
  ROM #(.addrWidth(12), .dataWidth(12)) rom_1 (.addr(Pc_q), .data(out_5));  // open: sel

  // Notes on the sheet:
  //   Individual Simulation:
  //   2) Per clock increment is 2. 
  //   1) First we need to click the clear pin.
  //   contents of rom_1 (hex, n*v repeats v):
  //   1c0 0 f4 0 f8 0 34a 0 0 0 68 0 68 0 4d4 0 316 0 2e8
  //   3) Instructions are stored in hexa format converting from binary to instruction memory(rom).
  //   OP 
  //   Instruction:(Binary)
  //   RS
  //   RT
  //   RD
  //   0001 11  00  00  00
  //   0000  11  11  01  00
  //   0000  11  11  10  00
  //   0011  01  00  11  10 
  //   0000  01  10  10  00 
  //   0000  01  10  10  00 
  //   0100  11  01  01  00
  //   0011  00  01  01  10
  //   0010  11  10  10  00
  //   5) We will click on the clock for the second time which will execute the add instruction. That is 0f4. It will write 0 at $t1.
  //   6) We will click on the clock for the sixth time which will execute the beq instruction. That is 316. It will compare $t0 & $t1(i,x).
  //   FUN
  //   Hexa
  //   1c0
  //   0f4
  //   0f8
  //   34a
  //   068
  //   068
  //   4d4
  //   316
  //   2e8
  //   4) We will click on the clock for the first time which will execute the load instruction. That is 1c0. It gets value from 0 no memory address and load the  value at $t0.
  //   7) We will click on the clock for the last time which will execute the store instruction. That is 2e8. It will store the ultimate sum result from $t2 to mem's(ram's) 8th memory address.
  //   Loop Execution
  //   lw $t0,0($zero)
  //   add $t1, $zero, $zero
  //   add $t2,$zero,$zero
  //   add &t2,&t2,&t1
  //   add $t2,$t2,$t1
  //   addi $t1,$t1,1
  //   sw $t2,4($zero)
  //   beq $t1 ,$t0,L2% compare i & x
  //   beq $zero,$zero,L1% go back to the loop
endmodule

// Instruction Decode
module ID (
  input  [11:0] in_1,
  input  [11:0] in_2,
  input  in_3,
  output [11:0] out_4,
  output [11:0] out_5,
  output [11:0] out_6,
  output F0,
  output F1,
  output Aludes,
  output RegWrite,
  output ID,
  output Str,
  output Bin,
  output Jump,
  output out_15
);

  wire controlunit_1_memreg, controlunit_1_regdes;
  wire [1:0] multiplexer_1_out;
  wire [2:0] bit_extender_1_out;

  controlunit controlunit_1 (
    .a(bit_extender_1_out[2]), .b(bit_extender_1_out[1]), .regdes(controlunit_1_regdes),
    .c(bit_extender_1_out[0]), .aludes(Aludes), .regwrite(RegWrite), .ld(ID), .str(Str),
    .memreg(controlunit_1_memreg), .bin(Bin), .jump(Jump), .addi(out_15));
  Bit_Extender #(.in_width(4), .out_width(3)) bit_extender_1 (.in(in_1[11:8]), .out(bit_extender_1_out));
  Multiplexer #(.width(2)) multiplexer_1 (
    .in0(in_1[3:2]), .in1(in_1[5:4]), .out(multiplexer_1_out), .sel(controlunit_1_regdes));  // open: en
  assign out_4 = {{8{1'b0}}, in_1[3:0]};  // Bit_Extender bit_extender_2
  \reg  reg_1 (
    .in_1(in_3), .in_2(multiplexer_1_out), .in_3(in_1[7:6]), .in_4(in_2), .in_5(controlunit_1_memreg),
    .in_6(in_1[5:4]), .out_7(out_5), .out_8(out_6));

  assign F0 = in_1[1];
  assign F1 = in_1[0];

  // Notes on the sheet:
  //   Individual Simulation:
  //   rs
  //   rt
  //   rd
  //   op
  //   fun
  //   imme
  //   2) For add instruction 0f4, my binary instructions are divided into rs,rt,rd,opcode and func. My 2X1 mux's selection pin regdes  will be off as add is a R type instruction. The instruction will write 0 to $t1. 
  //   3) For beq instruction 316, my binary instructions are divided into rs,rt,rd,opcode and func. My 2X1 mux's selection pin regdes will be on as beq is an I type instruction. The instruction will compare $t1 & $t0. If those are equal, there will be a jump. 
  //   4) For load instruction(2e8), my binary instructions are divided into rs,rt,rd,opcode and func. I have a mux which will define on which instruction I will work on. As store is an I instruction, the mux's select pin(regdes) will be high.In my 4 bit register file, the value of $t2 will be stored into my mem's 8th memory address.
  //   1) For load instruction(1c0), my binary instructions are divided into rs,rt,rd,opcode and func. I have a mux which will define on which instruction I will work on. As load is an I instruction, the mux's select pin(regdes) will be high.In my 4 bit register file, the loaded value will be shown in $t0. After working in register file, I got my read data 1 & 2.
endmodule

// Execute
module execution (
  input  in_1,
  input  [11:0] in_2,
  input  [11:0] in_3,
  input  Alu_Src,
  input  [11:0] in_5,
  input  Bin,
  input  F1,
  input  F0,
  output [11:0] out_9,
  output out_10,
  output [11:0] out_11
);

  wire n12_bit_alu_1_zero;
  wire [11:0] multiplexer_1_out;

  Multiplexer #(.width(12)) multiplexer_1 (.in0(in_3), .in1(in_5), .out(multiplexer_1_out), .sel(Alu_Src));  // open: en
  _12_bit_alu u_12_bit_alu_1 (
    .in_1(in_2), .in_7(multiplexer_1_out), .RESULT(out_11), .ZERO(n12_bit_alu_1_zero), .in_2(1'b0),
    .in_3(Bin), .in_4(1'b0), .in_5(F1), .in_6(F0));  // open: out_11, OVERFLOW
  and and_1 (out_10, in_1, n12_bit_alu_1_zero);

  assign out_9 = in_5;

  // Notes on the sheet:
  //   Individual Simulation:
  //   4) For store instruction(2e8), my register read data 2's value will directly go into mem's 8th memory address.
  //   2)For add instruction(0f4) , addition will be performed in alu. Read data 2 will enter into my alu as B after passing though 2X1 mux where the selection pin(alusrc) will be 0. Read data 1 will always work as A.
  //   1)For load instruction 1c0, the two read data will be controled by mux. For load the select pin of the 2X1 mux will be 1. I have connected it with alu and for load the add operation of alu will be performed. My f1 & f0 will be 0 for lw. 
  //   3) For beq instruction(316), extended immediate value from ID will go for 2 left shift. After that it will go to an adder. For that pcsrc will be high. In alu sub will be performed which will compare the 2 values of $t0 & t1. If the result is 0, those are equal and the zero flag will be 1. If both the zero flag and the jump instruction will be 1, a jump will occur. 
endmodule

// Mem
module mem (
  input  [11:0] in_1,
  input  [11:0] in_2,
  input  Clk,
  input  Mem_Write,
  input  Mem_Read,
  output [11:0] out_6
);

  RAM #(.addrWidth(12), .dataWidth(12), .bus("separate")) ram_1 (
    .addr(in_1), .din(in_2), .data(out_6), .str(Mem_Write), .clk(Clk), .ld(Mem_Read));  // open: sel, clr

  // Notes on the sheet:
  //   Individual Simulation:
  //   1) First I have clicked on the reset pin.
  //   3) For all instruction there will be no chnage At last my final sum will be stored at 8th memory address from $t2.
  //   4) For load instruction the mem write will be 0 and mem read will be 1. The value of my 0th memory address will move into $t0.
  //   2) The number of time I want my loop to execute I have loaded that number in 0th memory address. I have stored 001 in 4th memory address for addi
  //   5) For store instruction the mem write will be 1 and mem read will be 0. The register's read data 2 will be written into my ram's 8th memory address.
endmodule

// WB
module wb (
  input  [11:0] in_1,
  input  [11:0] in_2,
  input  memtoreg,
  output [11:0] out_4
);

  Multiplexer #(.width(12)) multiplexer_1 (.in0(in_1), .in1(in_2), .out(out_4), .sel(memtoreg));  // open: en

  // Notes on the sheet:
  //   Individual Simulation:
  //   3) For 316(beq instruction), write back is not required
  //   4) For 2e8(store instruction), write back is not required
  //   2) For 0f4(add instruction), memtoreg will be 1 so that the alu's addition result can get back into write data.
  //    1)For 1c0(the load instruction), memtoreg will be 1 so that the data will write back to instruction decode's write data pin.
endmodule

module datapath (
  input  Clear
);

  wire Clock_out, execution_1_out_10, id_1_aludes, id_1_bin, id_1_f0, id_1_f1, id_1_id, id_1_jump,
       id_1_out_15, id_1_regwrite, id_1_str;
  wire [11:0] execution_1_out_9, execution_1_out_11, id_1_out_4, id_1_out_5, id_1_out_6, if_1_out_5,
       mem_1_out_6, multiplexer_1_out, n12_bit_alu_1_result, wb_1_out_4;

  Clock Clock (.out(Clock_out));
  IF if_1 (.in_1(execution_1_out_9), .pcsrc(execution_1_out_10), .Reset(Clear), .Clock(Clock_out), .out_5(if_1_out_5));
  ID id_1 (
    .in_1(if_1_out_5), .Aludes(id_1_aludes), .RegWrite(id_1_regwrite), .ID(id_1_id), .Str(id_1_str),
    .Bin(id_1_bin), .out_15(id_1_out_15), .in_2(multiplexer_1_out), .out_5(id_1_out_5), .out_6(id_1_out_6),
    .in_3(Clock_out), .F0(id_1_f0), .F1(id_1_f1), .out_4(id_1_out_4), .Jump(id_1_jump));
  execution execution_1 (
    .in_1(id_1_jump), .in_2(id_1_out_5), .in_3(id_1_out_6), .Alu_Src(id_1_aludes), .in_5(id_1_out_4),
    .Bin(id_1_bin), .F1(id_1_f0), .F0(id_1_f1), .out_9(execution_1_out_9), .out_10(execution_1_out_10),
    .out_11(execution_1_out_11));
  mem mem_1 (
    .in_1(execution_1_out_11), .in_2(id_1_out_6), .Clk(Clock_out), .Mem_Write(id_1_str), .Mem_Read(id_1_id),
    .out_6(mem_1_out_6));
  wb wb_1 (.in_1(execution_1_out_11), .in_2(mem_1_out_6), .memtoreg(id_1_regwrite), .out_4(wb_1_out_4));
  _12_bit_alu u_12_bit_alu_1 (
    .in_1(id_1_out_6), .in_7(wb_1_out_4), .RESULT(n12_bit_alu_1_result), .in_2(1'b0), .in_3(1'b0),
    .in_4(1'b0), .in_5(1'b0), .in_6(1'b0));  // open: out_11, OVERFLOW, ZERO
  Multiplexer #(.width(12)) multiplexer_1 (
    .in0(wb_1_out_4), .in1(n12_bit_alu_1_result), .out(multiplexer_1_out), .sel(id_1_out_15));  // open: en

  // Notes on the sheet:
  //   Simulation Process(whole data-path):
  //   8) We need to do it again for sum=sum+2i.
  //   7)We will click on the clock again which will execute 068. It is for sum=sum+i.
  //   4) We will click on the clock again which will execute the instruction 0f4. It will write 0 value at $t1.
  //   5) We will click on the clock again which will execute the instruction 0f8. It will write 0 at $t2. 
  //   Opcode
  //   4 bit
  //   1) Before starting the simulation, we need to double click on the 'clear' pin which is connected with program counter(register.
  //   2) We will go to mem and add a value at 0 number address which is x and add 1 at 4th instruction for addi.
  //   Data Table 
  //   Rs
  //   2 bit
  //   6) We will click on the clock again which will execute the instruction 34a. It will compare $t1 & $t2's value and jump into 10th instruction.
  //   9) We will click on the clock again which will execute the instruction 4d4. It will add value from $t and 4 no memory address where I stored 1 earlier.
  //   Rd
  //   Rt
  //   2 bit
  //   2 bit
  //   3) We will click on the clock for the first time which will execute the load instruction. That is 1c0. It gets value from 0 no memory address and store the  value at $t0.
  //   11) We will click on the clock again which will execute the instruction 2e8. It will store $t2's value into ram's 8 no address. The stored value is the sum.
  //   Fun
  //   2 bit
  //   10) We will click on the clock again which will execute the instruction 316. It will compare $t1 &$t2's value. If they are not equal, it will go back to 6th instruction otherwise the loop will break and it will move to nect instruction.
  //   Loop Execution
  //   lw $t0,0($zero)
  //   add $t1, $zero, $zero
  //   add $t2,$zero,$zero
  //   beq $t1 ,$t0,L2% compare i & x
  //   add &t2,&t2,&t1
  //   add $t2,$t2,$t1
  //   addi $t1,$t1,1
  //   sw $t2,4($zero)
  //   beq $zero,$zero,L1% go back to the loop
endmodule

module Control (
  input  OP3,
  input  OP2,
  input  OP1,
  input  OP0,
  output Regdst,
  output Alusrc,
  output Memtoreq,
  output Regwrite,
  output Mem_Read,
  output Mem_Write,
  output Branch,
  output Aluop1,
  output Addi
);

  and R_Type (Regdst, ~OP3, ~OP2, ~OP1, ~OP1);  // AND_Gate
  and Lw (Mem_Read, ~OP3, ~OP2, ~OP1, OP0);  // AND_Gate
  and Sw (Mem_Write, ~OP3, ~OP2, OP1, OP1);  // AND_Gate
  and Beq (Aluop1, ~OP3, ~OP2, OP1, OP0);  // AND_Gate
  and u_Addi (Addi, ~OP3, OP2, ~OP1, ~OP0);  // AND_Gate
  or or_1 (Alusrc, Mem_Write, Mem_Read);
  or or_2 (Regwrite, Regdst, Mem_Read);

  assign Branch = Aluop1;
  assign Memtoreq = Mem_Read;
endmodule
